// Logisim project s1.t.21-logisim.circ as structural Verilog: 1 circuit, main circuit main
module main (
  input  Vacany_status,
  input  [3:0] Enter__Password,
  input  in_3,
  input  Vacany_status_2,
  input  [3:0] Enter__Password_2,
  input  Vacany_status_3,
  input  [3:0] Enter__Password_3,
  input  Vacany_status_4,
  input  [3:0] Enter__Password_4,
  input  Vacany_status_5,
  input  [3:0] Enter__Password_5,
  output [3:0] out_12,
  output Locker_open_status,
  output out_14,
  output [3:0] out_15,
  output Locker_open_status_2,
  output out_17,
  output [3:0] out_18,
  output Locker_open_status_3,
  output out_20,
  output [3:0] out_21,
  output Locker_open_status_4,
  output out_23,
  output [3:0] out_24,
  output Locker_open_status_5,
  output out_26
);

  wire decoder_1_out0, decoder_1_out1, decoder_1_out2, decoder_1_out3, decoder_1_out4, decoder_1_out5,
       decoder_1_out6, decoder_1_out7, decoder_1_out8, decoder_1_out9, decoder_1_out10, decoder_1_out11,
       decoder_1_out12, decoder_1_out13, decoder_1_out14, decoder_1_out15, decoder_1_out16, decoder_1_out17,
       decoder_1_out18, decoder_1_out19, decoder_1_out20, decoder_1_out21, decoder_1_out22, decoder_1_out23,
       decoder_1_out24, decoder_1_out25, decoder_1_out26, decoder_1_out27, decoder_1_out28, decoder_1_out29,
       decoder_1_out30, decoder_1_out31, not_6_out, not_7_out, not_8_out, not_9_out, not_10_out, or_1_out,
       or_2_out, or_3_out, or_4_out, Password_reset_2_out, Password_reset_3_out, Password_reset_4_out,
       Password_reset_5_out, Password_reset_out;
  wire [4:0] not_5_out;

  LED led_1 ();  // open: in
  LED led_2 ();  // open: in
  or or_1 (or_1_out, decoder_1_out2, decoder_1_out3);
  or or_2 (or_2_out, decoder_1_out4, decoder_1_out5, decoder_1_out6, decoder_1_out7);
  LED _1st_BOX (.in(or_4_out));
  LED _2nd_BOX (.in(or_3_out));
  LED _3RD_BOX (.in(or_2_out));
  LED led_3 (.in(or_1_out));
  LED led_4 (.in(decoder_1_out1));
  LED led_5 (.in(decoder_1_out0));
  or or_3 (or_3_out, decoder_1_out8, decoder_1_out9, decoder_1_out10, decoder_1_out11, decoder_1_out12, decoder_1_out13, decoder_1_out14, decoder_1_out15);
  or or_4 (or_4_out, decoder_1_out23, decoder_1_out16, decoder_1_out17, decoder_1_out18, decoder_1_out19, decoder_1_out20, decoder_1_out21, decoder_1_out22, decoder_1_out24, decoder_1_out25, decoder_1_out26, decoder_1_out27, decoder_1_out28, decoder_1_out29, decoder_1_out30, decoder_1_out31);
  Decoder #(.select(5)) decoder_1 (
    .out0(decoder_1_out0), .out1(decoder_1_out1), .out2(decoder_1_out2), .out3(decoder_1_out3),
    .out4(decoder_1_out4), .out5(decoder_1_out5), .out6(decoder_1_out6), .out7(decoder_1_out7),
    .out8(decoder_1_out8), .out9(decoder_1_out9), .out10(decoder_1_out10), .out11(decoder_1_out11),
    .out12(decoder_1_out12), .out13(decoder_1_out13), .out14(decoder_1_out14), .out15(decoder_1_out15),
    .out16(decoder_1_out16), .out17(decoder_1_out17), .out18(decoder_1_out18), .out19(decoder_1_out19),
    .out20(decoder_1_out20), .out21(decoder_1_out21), .out22(decoder_1_out22), .out23(decoder_1_out23),
    .out24(decoder_1_out24), .out25(decoder_1_out25), .out26(decoder_1_out26), .out27(decoder_1_out27),
    .out28(decoder_1_out28), .out29(decoder_1_out29), .out30(decoder_1_out30), .out31(decoder_1_out31),
    .sel(not_5_out));  // open: en
  not not_1 (not_5_out[4], Vacany_status);
  not not_2 (not_5_out[3], Vacany_status_2);
  not not_3 (not_5_out[2], Vacany_status_3);
  not not_4 (not_5_out[1], Vacany_status_4);
  not not_5 (not_5_out[0], Vacany_status_5);
  LED led_6 (.in(Vacany_status));
  LED led_7 (.in(Vacany_status_2));
  LED led_8 (.in(Vacany_status_3));
  LED led_9 (.in(Vacany_status_4));
  LED led_10 (.in(Vacany_status_5));
  Button Password_reset (.out(Password_reset_out));
  Button Password_reset_2 (.out(Password_reset_2_out));
  Button Password_reset_3 (.out(Password_reset_3_out));
  Button Password_reset_4 (.out(Password_reset_4_out));
  Button Password_reset_5 (.out(Password_reset_5_out));
  Random #(.width(4)) random_1 (.clk(Password_reset_3_out), .out(out_18));  // open: next, clr
  Random #(.width(4)) random_2 (.clk(Password_reset_4_out), .out(out_21));  // open: next, clr
  Random #(.width(4)) random_3 (.clk(Password_reset_5_out), .out(out_24));  // open: next, clr
  Random #(.width(4)) random_4 (.clk(Password_reset_out), .out(out_12));  // open: next, clr
  Random #(.width(4)) random_5 (.clk(Password_reset_2_out), .out(out_15));  // open: next, clr
  Comparator #(.width(4), .mode("unsigned")) comparator_1 (
    .a(out_12), .b(Enter__Password), .eq(out_14));  // open: gt, lt
  Comparator #(.width(4), .mode("unsigned")) comparator_2 (
    .a(out_15), .b(Enter__Password_2), .eq(out_17));  // open: gt, lt
  Comparator #(.width(4), .mode("unsigned")) comparator_3 (
    .a(out_18), .b(Enter__Password_3), .eq(out_20));  // open: gt, lt
  Comparator #(.width(4), .mode("unsigned")) comparator_4 (
    .a(out_21), .b(Enter__Password_4), .eq(out_23));  // open: gt, lt
  Comparator #(.width(4), .mode("unsigned")) comparator_5 (
    .a(out_24), .b(Enter__Password_5), .eq(out_26));  // open: gt, lt
  not not_6 (not_6_out, Vacany_status);
  not not_7 (not_7_out, Vacany_status_2);
  not not_8 (not_8_out, Vacany_status_3);
  not not_9 (not_9_out, Vacany_status_4);
  not not_10 (not_10_out, Vacany_status_5);
  or or_5 (Locker_open_status, not_6_out, out_14);
  or or_6 (Locker_open_status_2, not_7_out, out_17);
  or or_7 (Locker_open_status_3, not_8_out, out_20);
  or or_8 (Locker_open_status_4, not_9_out, out_23);
  or or_9 (Locker_open_status_5, not_10_out, out_26);

  // Notes on the sheet:
  //   NAVANEET MURALI - 231CS136
  //   NIHAL RAJ MATURI - 231CS138
  //   DDS MINI PROJECT-S1-T21:
  //   AUTOMATED DELIVERY LOCKER SYSTEM
  //   BALAGOPAL NAGULAGAMA - 231CS135
  //                          INSTRUCTIONS FOR DELIVERY AGENT:
  //   -Indicates Locker is available
  //   compartment in which package was placed.
  //   INTRUCTIONS FOR THE RECEIVER:
  //   -Indicates Locker is occupied
  //    green is the compartment that package should be placed in.
  //   1.Enter the assigned password in the assigned compartment to unlock. 
  //   2.Take the package out and click the vacant status button.
  //   1.Check for the display colour of the respective compartments. The one that displays
  //   3.After placing the parcel, click the vacant status button present adjacent to the
  //   2. Place the package in the assigned compartment and lock the door using password reset button.
  //                       NO VACANCY
  //                 4TH BOX
  //               5TH BOX
  //   password is correct
  //   password is correct
  //   password is correct
  //   password is correct
  //   password is correct
  //   Compartment-1
  //   Compartment-2
  //   Compartment-3
  //   Compartment-4
  //   Compartment-5
endmodule
